// Logisim project mar.circ as structural Verilog
module main (
);

  wire clock_1_out, demultiplexer_1_out1, demultiplexer_1_out4;
  wire [1:0] controlunit_1_mw;
  wire [2:0] controlunit_1_p0, controlunit_1_p3;
  wire [3:0] multiplexer_1_out, multiplexer_1_out_2, multiplexer_1_out_3, multiplexer_1_out_4;
  wire [11:0] MAR_q;
  wire [15:0] AC_q, ram_1_dout, undriven, undriven_2, undriven_3, undriven_4, undriven_5;

  Clock clock_1 (.out(clock_1_out));
  Demultiplexer #(.select(3)) demultiplexer_1 (
    .out1(demultiplexer_1_out1), .out4(demultiplexer_1_out4), .in(1'b1), .sel(controlunit_1_p3));  // open: out0, out2, out3, out5, out6, out7
  RAM #(.addrWidth(12), .dataWidth(16)) ram_1 (
    .addr(MAR_q), .we(controlunit_1_mw[0]), .oe(controlunit_1_mw[1]), .clk(clock_1_out),
    .din({multiplexer_1_out_4, multiplexer_1_out_3, multiplexer_1_out_2, multiplexer_1_out}),
    .dout(ram_1_dout));
  Register #(.width(12)) MAR (.D(12'h5), .en(demultiplexer_1_out1), .clk(clock_1_out), .Q(MAR_q));  // open: clr
  Register #(.width(16)) AC (.D({16{1'b0}}), .en(demultiplexer_1_out4), .clk(clock_1_out), .Q(AC_q));  // open: clr
  ControlUnit controlunit_1 (
    .P0(controlunit_1_p0[0]), .P1(controlunit_1_p0[1]), .P2(controlunit_1_p0[2]), .P3(controlunit_1_p3[0]),
    .P4(controlunit_1_p3[1]), .P5(controlunit_1_p3[2]), .Mr(controlunit_1_mw[1]), .Mw(controlunit_1_mw[0]));  // open: En, RingCounter, IRopcode, A0, A1, Cr, Lalt
  Multiplexer #(.select(3), .width(16)) multiplexer_1 (
    .in0(ram_1_dout), .in1({4'b0000, MAR_q}), .in2(undriven_2), .in3(undriven), .in4(AC_q), .in5(undriven_3),
    .in6(undriven_4), .in7(undriven_5),
    .out({multiplexer_1_out_4, multiplexer_1_out_3, multiplexer_1_out_2, multiplexer_1_out}),
    .sel(controlunit_1_p0));
  Hex_Digit_Display hex_digit_display_1 (.value(multiplexer_1_out_4));  // open: dp
  Hex_Digit_Display hex_digit_display_2 (.value(multiplexer_1_out_3));  // open: dp
  Hex_Digit_Display hex_digit_display_3 (.value(multiplexer_1_out_2));  // open: dp
  Hex_Digit_Display hex_digit_display_4 (.value(multiplexer_1_out));  // open: dp

  // Notes on the sheet:
  //   p5 p4 p3
  //   p2 p1 p0
  //   Data Bus
endmodule

module cyclecount (
  input  Clock,
  input  Cr,
  output T0,
  output T1,
  output T2,
  output T3,
  output T4
);

  or or_1 (T0, T4, T3, T2, T1);
  D_Flip_Flop D0 (.D(T0), .clk(Clock), .Q(T1), .reset(Cr));  // open: Qn, preset
  D_Flip_Flop D1 (.D(T1), .clk(Clock), .Q(T2), .reset(Cr));  // open: Qn, preset
  D_Flip_Flop D2 (.D(T2), .clk(Clock), .Q(T3), .reset(Cr));  // open: Qn, preset
  D_Flip_Flop D3 (.D(T3), .clk(Clock), .Q(T4), .reset(Cr));  // open: Qn, preset

  // Notes on the sheet:
  //   clock
  //   Cr
endmodule

module testkeyboard (
  input  b0,
  input  b1,
  input  b2,
  input  b3,
  input  b4,
  input  b5,
  input  b6,
  input  b7,
  input  b8,
  input  b9,
  input  bA,
  input  bB,
  input  bC,
  input  bD,
  input  bE,
  input  bF,
  output [3:0] keyout
);

  Priority_Encoder #(.select(4)) priority_encoder_1 (
    .in0(b0), .in1(b1), .in2(b2), .in3(b3), .in4(b4), .in5(b5), .in6(b6), .in7(b7), .in8(b8), .in9(b9),
    .in10(bA), .in11(bB), .in12(bC), .in13(bD), .in14(bE), .in15(bF), .out(keyout));  // open: gs, en_out, en_in
endmodule

module ControlUnit (
  input  En,
  input  [7:0] RingCounter,
  input  [3:0] IRopcode,
  output P0,
  output P1,
  output P2,
  output P3,
  output P4,
  output P5,
  output A0,
  output A1,
  output Cr,
  output Mr,
  output Mw,
  output Lalt
);

  wire decoder_1_out0, decoder_1_out1, decoder_1_out2, decoder_1_out3, decoder_1_out4, decoder_1_out5,
       decoder_1_out6, decoder_1_out7, decoder_1_out8, decoder_1_out9, decoder_1_out10, decoder_1_out11,
       decoder_1_out12, decoder_1_out13, decoder_1_out14, decoder_1_out15;

  Decoder #(.select(4)) decoder_1 (
    .out0(decoder_1_out0), .out1(decoder_1_out1), .out2(decoder_1_out2), .out3(decoder_1_out3),
    .out4(decoder_1_out4), .out5(decoder_1_out5), .out6(decoder_1_out6), .out7(decoder_1_out7),
    .out8(decoder_1_out8), .out9(decoder_1_out9), .out10(decoder_1_out10), .out11(decoder_1_out11),
    .out12(decoder_1_out12), .out13(decoder_1_out13), .out14(decoder_1_out14), .out15(decoder_1_out15),
    .sel(IRopcode), .en(En));
  Load load_1 (
    .EN(decoder_1_out1), .RingCounter(RingCounter), .P0(P0), .P1(P1), .P2(P2), .P3(P3), .P4(P4), .P5(P5),
    .A0(A0), .A1(A1), .Cr(Cr), .Mr(Mr), .Mw(Mw), .Lalt(Lalt));
  BaseOp baseop_1 (
    .EN(decoder_1_out2), .RingCounter(RingCounter), .P0(P0), .P1(P1), .P2(P2), .P3(P3), .P4(P4), .P5(P5),
    .A0(A0), .A1(A1), .Cr(Cr), .Mr(Mr), .Mw(Mw), .Lalt(Lalt));
  Add add_1 (
    .En(decoder_1_out3), .RingCounter(RingCounter), .P0(P0), .P1(P1), .P2(P2), .P3(P3), .P4(P4), .P5(P5),
    .A0(A0), .A1(A1), .Cr(Cr), .Mr(Mr), .Mw(Mw), .Lalt(Lalt));
  BaseOp baseop_2 (
    .EN(decoder_1_out4), .RingCounter(RingCounter), .P0(P0), .P1(P1), .P2(P2), .P3(P3), .P4(P4), .P5(P5),
    .A0(A0), .A1(A1), .Cr(Cr), .Mr(Mr), .Mw(Mw), .Lalt(Lalt));
  BaseOp baseop_3 (
    .EN(decoder_1_out5), .RingCounter(RingCounter), .P0(P0), .P1(P1), .P2(P2), .P3(P3), .P4(P4), .P5(P5),
    .A0(A0), .A1(A1), .Cr(Cr), .Mr(Mr), .Mw(Mw), .Lalt(Lalt));
  BaseOp baseop_4 (
    .EN(decoder_1_out6), .RingCounter(RingCounter), .P0(P0), .P1(P1), .P2(P2), .P3(P3), .P4(P4), .P5(P5),
    .A0(A0), .A1(A1), .Cr(Cr), .Mr(Mr), .Mw(Mw), .Lalt(Lalt));
  BaseOp baseop_5 (
    .EN(decoder_1_out7), .RingCounter(RingCounter), .P0(P0), .P1(P1), .P2(P2), .P3(P3), .P4(P4), .P5(P5),
    .A0(A0), .A1(A1), .Cr(Cr), .Mr(Mr), .Mw(Mw), .Lalt(Lalt));
  BaseOp baseop_6 (
    .EN(decoder_1_out8), .RingCounter(RingCounter), .P0(P0), .P1(P1), .P2(P2), .P3(P3), .P4(P4), .P5(P5),
    .A0(A0), .A1(A1), .Cr(Cr), .Mr(Mr), .Mw(Mw), .Lalt(Lalt));
  BaseOp baseop_7 (
    .EN(decoder_1_out9), .RingCounter(RingCounter), .P0(P0), .P1(P1), .P2(P2), .P3(P3), .P4(P4), .P5(P5),
    .A0(A0), .A1(A1), .Cr(Cr), .Mr(Mr), .Mw(Mw), .Lalt(Lalt));
  BaseOp baseop_8 (
    .EN(decoder_1_out10), .RingCounter(RingCounter), .P0(P0), .P1(P1), .P2(P2), .P3(P3), .P4(P4), .P5(P5),
    .A0(A0), .A1(A1), .Cr(Cr), .Mr(Mr), .Mw(Mw), .Lalt(Lalt));
  BaseOp baseop_9 (
    .EN(decoder_1_out11), .RingCounter(RingCounter), .P0(P0), .P1(P1), .P2(P2), .P3(P3), .P4(P4), .P5(P5),
    .A0(A0), .A1(A1), .Cr(Cr), .Mr(Mr), .Mw(Mw), .Lalt(Lalt));
  BaseOp baseop_10 (
    .EN(decoder_1_out12), .RingCounter(RingCounter), .P0(P0), .P1(P1), .P2(P2), .P3(P3), .P4(P4), .P5(P5),
    .A0(A0), .A1(A1), .Cr(Cr), .Mr(Mr), .Mw(Mw), .Lalt(Lalt));
  BaseOp baseop_11 (
    .EN(decoder_1_out13), .RingCounter(RingCounter), .P0(P0), .P1(P1), .P2(P2), .P3(P3), .P4(P4), .P5(P5),
    .A0(A0), .A1(A1), .Cr(Cr), .Mr(Mr), .Mw(Mw), .Lalt(Lalt));
  BaseOp baseop_12 (
    .EN(decoder_1_out14), .RingCounter(RingCounter), .P0(P0), .P1(P1), .P2(P2), .P3(P3), .P4(P4), .P5(P5),
    .A0(A0), .A1(A1), .Cr(Cr), .Mr(Mr), .Mw(Mw), .Lalt(Lalt));
  BaseOp baseop_13 (
    .EN(decoder_1_out15), .RingCounter(RingCounter), .P0(P0), .P1(P1), .P2(P2), .P3(P3), .P4(P4), .P5(P5),
    .A0(A0), .A1(A1), .Cr(Cr), .Mr(Mr), .Mw(Mw), .Lalt(Lalt));

  // Notes on the sheet:
  //   P0
  //   P1
  //   P2
  //   P3
  //   P4
  //   P5
  //   A0
  //   A1
  //   Cr
  //   Mr
  //   Mw
  //   Lalt
endmodule

module Add (
  input  En,
  input  [7:0] RingCounter,
  output P0,
  output P1,
  output P2,
  output P3,
  output P4,
  output P5,
  output A0,
  output A1,
  output Cr,
  output Mr,
  output Mw,
  output Lalt
);

  and and_1 (P0, RingCounter[3], En);
  and and_2 (Mr, RingCounter[4], En);
  and and_3 (A0, En, En);
  or out3 (P3, P0, Mr);

  assign A1 = 1'b0;
  assign Cr = A0;
  assign Lalt = A0;
  assign Mw = 1'b0;
  assign P1 = P0;
  assign P2 = P0;
  assign P4 = Mr;
  assign P5 = A0;
  assign RingCounter[5] = En;

  // Notes on the sheet:
  //   ADD=0011
endmodule

module BaseOp (
  input  EN,
  input  [7:0] RingCounter,
  output P0,
  output P1,
  output P2,
  output P3,
  output P4,
  output P5,
  output A0,
  output A1,
  output Cr,
  output Mr,
  output Mw,
  output Lalt
);
endmodule

module Load (
  input  EN,
  input  [7:0] RingCounter,
  output P0,
  output P1,
  output P2,
  output P3,
  output P4,
  output P5,
  output A0,
  output A1,
  output Cr,
  output Mr,
  output Mw,
  output Lalt
);

  // AND_Gate and_1 has open pins: in0=RingCounter[5], in1=EN, out=open
  // AND_Gate and_2 has open pins: in0=RingCounter[4], in1=EN, out=open
  // AND_Gate and_3 has open pins: in0=RingCounter[3], in1=EN, out=open
endmodule
